# Fritzing sketch Sketch (saved by Fritzing 0.8.3b)
breadboards: 1

parts:
  Componente1 = Arduino Uno (Rev3)
  R1 = Resistor [tolerance=±5% resistance=220 package=THT]
  Componente2 = Max Power IR LED Kit [part_number=transmitter]
  Componente3 = Max Power IR LED Kit  # not connected

nets:
  N1: Componente1.GND, Componente2.CONTROL
  N2: Componente1.D3_PWM, R1.Pin_1
  5V: Componente1.5V, Componente2.VCC
